# Fritzing sketch Esquema de Conexiones Arduino (saved by Fritzing 0.9.3b)
breadboards: 1

parts:
  U1 = ESP32S-HiLetgo [part_number=ESP32S-HiLetgo]
  U2 = GAS_SENSOR [package=mq-3]
  DHT1 = DHT22 Humidity and Temperature Sensor
  WeMos_D1_Mini_Relay_Shield_V1 = WeMos D1 Mini Relay Shield V2
  WeMos_D1_Mini_Relay_Shield_V2 = WeMos D1 Mini Relay Shield V2

nets:
  N1: U1.3.3, DHT1.VDD
  N2: U1.GPIO25, WeMos_D1_Mini_Relay_Shield_V1.D7
  N3: U1.GPIO26, WeMos_D1_Mini_Relay_Shield_V2.D7
  3V3: U1.VIN, U2.H2, WeMos_D1_Mini_Relay_Shield_V1.3V3, WeMos_D1_Mini_Relay_Shield_V2.3V3
  N4: U1.GPIO16, DHT1.DATA
  GND: U1.GND, U2.H1, DHT1.GND, WeMos_D1_Mini_Relay_Shield_V1.D8, WeMos_D1_Mini_Relay_Shield_V2.D8

custom parts:
  ESP32S-HiLetgo: HiLetgo ESP-WROOM-32 ESP32 ESP-32S Development Board 2.4GHz Dual-Mode WiFi + Bluetooth Dual Cores Microcontroller The ESP32 integrated with Antenna switches, RF Balun, power amplifiers, low-noise amplifiers, filters, and management modules, and the entire solution occupies the least area of PCB. 2.4 GHz Wi-Fi plus Bluetooth dual-mode chip, with TSMC Ultra-low power consumption 40nm technology,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
